# Fritzing sketch decimal_to_binary (saved by Fritzing 0.9.4)
breadboards: 1

parts:
  Nano1 = Arduino Nano v2.3
  LED1 = LED - 5mm [color="Red (633nm)" package="5 mm [THT]"]
  LED2 = LED - 5mm [color="Red (633nm)" package="5 mm [THT]"]
  LED3 = LED - 5mm [color="Red (633nm)" package="5 mm [THT]"]
  LED4 = LED - 5mm [color="Red (633nm)" package="5 mm [THT]"]
  R1 = Resistor [tolerance=±5% resistance=220 package=THT]
  R2 = Resistor [tolerance=±5% resistance=220 package=THT]
  R3 = Resistor [tolerance=±5% resistance=220 package=THT]
  R4 = Resistor [tolerance=±5% resistance=220 package=THT]

nets:
  N1: Nano1.GND, R1.Pin_1, R2.Pin_1, R3.Pin_1, R4.Pin_1
  N2: Nano1.D2, LED1.anode
  N3: Nano1.D3, LED2.anode
  N4: Nano1.D4, LED3.anode
  N5: Nano1.D5, LED4.anode
  N6: LED1.cathode, R1.Pin_0
  N7: LED2.cathode, R2.Pin_0
  N8: LED3.cathode, R3.Pin_0
  N9: LED4.cathode, R4.Pin_0
